# Fritzing sketch Clock (saved by Fritzing 0.9.3b)
breadboards: 2

parts:
  Onderdeel1 = Arduino Uno (Rev3)
  R1 = Rotary Potentiometer (Large) [maximum_resistance=100kΩ package=THT]
  LCD1 = LCD screen
  ZS-042_RTC1 = ZS-042 RTC Module  # not connected

nets:
  N1: Onderdeel1.D11_PWM/MOSI, LCD1.RS
  N2: Onderdeel1.D12/MISO, LCD1.E
  N3: Onderdeel1.D2, LCD1.DB4
  N4: Onderdeel1.D3_PWM, LCD1.DB5
  N5: Onderdeel1.D4, LCD1.DB6
  N6: Onderdeel1.D5_PWM, LCD1.DB7
  5V: Onderdeel1.5V, R1.leg1, LCD1.VDD, LCD1.LED+
  GND: Onderdeel1.GND, R1.leg2, LCD1.VSS, LCD1.R/W, LCD1.LED-
  N7: R1.wiper, LCD1.V0
